// Digital circuit alu.dig as structural Verilog
module alu (
  input  [3:0] a,
  input  [3:0] b,
  input  invert,
  input  arith,
  input  pass,
  input  cin,
  output [3:0] y,
  output cout,
  output overfl
);

  wire [3:0] not_neg_1_y;

  not_neg not_neg_1 (.a(a), .invert(invert), .neg(arith), .y(not_neg_1_y));  // open: cry
  and_add and_add_1 (
    .a(not_neg_1_y), .b(b), .add(arith), .cin(cin), .pass(pass), .y(y), .cout(cout), .overflow(overfl));
endmodule
