// Digital circuit and_add.dig as structural Verilog
module and_add (
  input  [3:0] a,
  input  [3:0] b,
  input  add,
  input  cin,
  input  pass,
  output [3:0] y,
  output cout,
  output overflow
);

  wire [3:0] and_1_out, four_bit_adder_1_y, four_bit_mux_1_y;

  four_bit_adder four_bit_adder_1 (.a(a), .b(b), .cin(cin), .y(four_bit_adder_1_y), .cout(cout), .overfl(overflow));
  and and_1 (and_1_out[3], a[3], b[3]);
  and and_2 (and_1_out[2], a[2], b[2]);
  and and_3 (and_1_out[1], a[1], b[1]);
  and and_4 (and_1_out[0], a[0], b[0]);
  four_bit_mux four_bit_mux_1 (.a(and_1_out), .b(four_bit_adder_1_y), .sel(add), .y(four_bit_mux_1_y));
  four_bit_mux four_bit_mux_2 (.a(four_bit_mux_1_y), .b(a), .sel(pass), .y(y));
endmodule
