// Digital circuit circuit addr_gen.dig as structural Verilog
module circuit_addr_gen (
  input  reset,
  input  [3:0] data__bus,
  input  load__mar,
  input  clk,
  input  use__pc,
  output [3:0] addr__bus
);

  wire not_1_out;
  wire [3:0] mar, pc;

  program_ctr program_ctr_1 (.enable(use__pc), .reset(reset), .clk(clk), .q(pc));
  four_bit_reg u_MAR (.d(data__bus), .enable(load__mar), .reset(reset), .clk(clk), .q(mar));
  not not_1 (not_1_out, use__pc);
  four_bit_mux four_bit_mux_1 (.a(pc), .b(mar), .sel(not_1_out), .y(addr__bus));
endmodule
