// Digital circuit controller.dig as structural Verilog
module controller (
);

  ROM #(.AddrBits(6), .Bits(14)) microcode_ROM ();  // open: A, sel, D

  // Notes on the sheet:
  //   contents of microcode_ROM (hex, n*v repeats v):
  //   1205,234,0,0,1205,294,0,0,1205,1000,0,0,1205,0,0,0,1205,0,0,0
  //   ,1205,0,0,0,1205,0,0,0,1205,0,0,3fff
endmodule
