// Digital circuit incrementer.dig as structural Verilog
module incrementer (
  input  [3:0] a,
  input  inc,
  output [3:0] y,
  output cry
);

  wire half_adder_2_cry, half_adder_3_cry, half_adder_4_cry;

  half_adder half_adder_1 (.a(a[3]), .b(half_adder_2_cry), .sum(y[3]), .cry(cry));
  half_adder half_adder_2 (.a(a[2]), .b(half_adder_3_cry), .sum(y[2]), .cry(half_adder_2_cry));
  half_adder half_adder_3 (.a(a[1]), .b(half_adder_4_cry), .sum(y[1]), .cry(half_adder_3_cry));
  half_adder half_adder_4 (.a(a[0]), .b(inc), .sum(y[0]), .cry(half_adder_4_cry));

  // Notes on the sheet:
  //   cry: cry
endmodule
