// Digital circuit program_ram.dig as structural Verilog
module program_ram (
  input  [3:0] addr,
  input  [3:0] data__in,
  input  clk,
  input  write,
  output [3:0] data__out
);

  RAMDualPort #(.AddrBits(4), .isProgramMemory("true"), .Bits(4)) ramdualport_1 (
    .A(addr), .Din(data__in), .str(write), .C(clk), .ld(1'b1), .D(data__out));
endmodule
